# Fritzing sketch bulldog_arduino_test_1 (saved by Fritzing 0.8.5b)
breadboards: 1

parts:
  IC1 = L293D [package=THT]
  M1 = DC Motor
  M2 = DC Motor
  Part1 = Arduino Uno (Rev3)
  BAT1 = Battery Holders [package=battery-aa]
  BAT2 = Battery Holders [package=battery-aa]

nets:
  N1: IC1.Enable_1, IC1.Enable_2, Part1.D10_PWM/SS
  N2: IC1.In_1, Part1.D4
  N3: IC1.Out_1_(_Controlled_by_Enable_1_), M2.pin_2
  N4: IC1.0V, Part1.GND, BAT1.+, BAT2.+
  N5: IC1.Out_2_(_Controlled_by_Enable_1_), M2.pin_1
  N6: IC1.In_2, Part1.D3_PWM
  N7: IC1.+Vmotor, BAT1.-
  N8: IC1.In_3, Part1.D5_PWM
  N9: IC1.Out_3_(_Controlled_by_Enable_2_), M1.pin_2
  N10: IC1.Out_4_(_Controlled_by_Enable_2_), M1.pin_1
  N11: IC1.In_4, Part1.D6_PWM
  N12: IC1.+V, Part1.5V
  N13: Part1.VIN, BAT2.-
